# Fritzing sketch Rookvat_schematic (saved by Fritzing 0.8.7b)
circuit board: 8.46667cm x 5.64444cm
breadboards: 1

parts:
  MenuSelector = Rotary Encoder [package=THT]
  Onderdeel1 = Arduino Mega 2560 (Rev3)
  MenuButton = Pushbutton [package=THT]
  R1 = Resistor [tolerance=±5% resistance=4.7k package=THT]
  LED1 = RGB LED (com. anode, rbg) [package="5 mm [THT]"]
  Speaker = Piezo Speaker
  Motor_rotation_check = Rotary Encoder [package=THT]
  Gas_Valve_Stepper_Motor = Stepper Motor - Bipolar
  R3 = Resistor [tolerance=±1% resistance=1k package=THT]
  LCD_TFT_2_2" = nokia5110
  R4 = Resistor [tolerance=±2% resistance=47k package=THT]
  R5 = Resistor [tolerance=±2% resistance=47k package=THT]
  R6 = Resistor [tolerance=±2% resistance=47k package=THT]
  R7 = Resistor [tolerance=±2% resistance=47k package=THT]
  Smoke_Valve_Servo = Basic Servo
  Stepper_motor_driver_(GasValve) = ULN2003A [package="SO16 [SMD]"]
  Real_Time_Clock = DS1307 [package=so08]
  R10 = Resistor [tolerance=±5% resistance=10k package=THT]
  R11 = Resistor [tolerance=±5% resistance=10k package=THT]
  R12 = Resistor [tolerance=±5% resistance=1k package=THT]
  R13 = Resistor [tolerance=±5% resistance=10k package=THT]
  SD_Card_(in_LCD_panel) = microSD Socket [package=usd-socket-pp]
  R14 = Resistor [tolerance=±2% resistance=220 package=THT]
  R15 = Resistor [tolerance=±5% resistance=220 package=THT]
  R16 = Resistor [tolerance=±5% resistance=470 package=THT]
  C1 = Ceramic Capacitor [capacitance=100nF package="100 mil [THT, multilayer]"]
  Pause = Pushbutton [package=THT]
  C2 = Ceramic Capacitor [capacitance=100nF package="100 mil [THT, multilayer]"]
  R17 = Resistor [tolerance=±5% resistance=10k package=THT]
  R18 = Resistor [tolerance=±2% resistance=47k package=THT]
  R19 = Resistor [tolerance=±5% resistance=47k package=THT]
  Ambiant_temp = DS18B20 1-Wire Temperature Sensor [part_number=DS18B20]
  Barrel_Temp = Temperature Sensor (Thermistor) [thermistor_type=NTC package=THT]
  Meat_Temp = Temperature Sensor (Thermistor) [thermistor_type=NTC package=THT]
  R22 = Resistor [tolerance=±5% resistance=68k package=THT]
  R23 = Resistor [tolerance=±5% resistance=68k package=THT]
  C3 = Ceramic Capacitor [capacitance=22µF package="100 mil [THT, multilayer]"]
  C4 = Ceramic Capacitor [capacitance=22µF package="100 mil [THT, multilayer]"]
  Thermocouple = IC, DIP package, 14 pins [chip_label=AD595CQ]
  C5 = Ceramic Capacitor [capacitance=0.1µF package="100 mil [THT, multilayer]"]
  Thermocouple_2 = Header 2 [package=springterminal-2.54mm-2]
  R24 = Resistor [tolerance=±5% resistance=68k package=THT]
  R25 = Resistor [tolerance=±5% resistance=68k package=THT]

nets (from the schematic view):
  N1: MenuSelector.EncoderPinA, Onderdeel1.D27
  VCC: MenuSelector.EncoderPinC, Onderdeel1.5V, R1.Pin_0, LED1.common_anode, Motor_rotation_check.EncoderPinC, Smoke_Valve_Servo.vcc, Real_Time_Clock.VCC, R10.Pin_0, R11.Pin_0, Pause.leg1, C2.1, R22.Pin_1, R23.Pin_1, Thermocouple.pin11, C5.1, R24.Pin_1, R25.Pin_1
  N2: MenuSelector.EncoderPinB, Onderdeel1.D19/RX1
  N3: Onderdeel1.A2, Motor_rotation_check.EncoderPinA
  N4: Onderdeel1.A3, Pause.leg0, C2.0, R17.Pin_1
  N5: Onderdeel1.A4, Meat_Temp.pin_1, R22.Pin_0, C3.1, R24.Pin_0
  N6: Onderdeel1.A5, Barrel_Temp.pin_1, R23.Pin_0, C4.1, R25.Pin_0
  N7: Onderdeel1.A6, Thermocouple.pin8, Thermocouple.pin9
  N8: Onderdeel1.D21/SCL, Onderdeel1.SCL, Real_Time_Clock.SCL, R11.Pin_1
  N9: Onderdeel1.D18/TX1, MenuButton.leg0, R13.Pin_0, C1.0
  N10: Onderdeel1.SDA, Real_Time_Clock.SDA, R10.Pin_1
  GND: Onderdeel1.GND, Speaker.pin2, LCD_TFT_2_2".Grnd, Smoke_Valve_Servo.gnd, Real_Time_Clock.GND, R13.Pin_1, R17.Pin_0, Ambiant_temp.GND, Barrel_Temp.pin_0, Meat_Temp.pin_0, C3.0, C4.0, Thermocouple.pin1, Thermocouple.pin4, Thermocouple.pin7, Thermocouple.pin13, C5.0, Thermocouple_2.2
  N11: Onderdeel1.D12_PWM, R16.Pin_0
  N12: Onderdeel1.D11_PWM, R15.Pin_0
  N13: Onderdeel1.D10_PWM, R14.Pin_0
  N14: Onderdeel1.D9_PWM, R12.Pin_0
  3V3: Onderdeel1.3V3, LCD_TFT_2_2".Vcc, LCD_TFT_2_2".LED
  N15: Onderdeel1.D3_PWM, R1.Pin_1, Ambiant_temp.DQ
  N16: Onderdeel1.D23, Stepper_motor_driver_(GasValve).In_1
  N17: Onderdeel1.D24, Stepper_motor_driver_(GasValve).In_2
  N18: Onderdeel1.D25, Stepper_motor_driver_(GasValve).In_3
  N19: Onderdeel1.D26, Stepper_motor_driver_(GasValve).In_4
  N20: Onderdeel1.D37, R3.Pin_0
  N21: Onderdeel1.D38, Motor_rotation_check.EncoderPinB
  N22: Onderdeel1.D47, R19.Pin_1
  N23: Onderdeel1.D48, R7.Pin_1
  N24: Onderdeel1.D49, R6.Pin_1
  N25: Onderdeel1.D51, R5.Pin_1
  N26: Onderdeel1.D52, R4.Pin_1
  N27: Onderdeel1.D53, R18.Pin_1
  N28: MenuButton.leg1, C1.1
  N29: LED1.red_cathode, R16.Pin_1
  N30: LED1.blue_cathode, R14.Pin_1
  N31: LED1.green_cathode, R15.Pin_1
  N32: Speaker.pin1, R3.Pin_1
  N33: Gas_Valve_Stepper_Motor.A, Stepper_motor_driver_(GasValve).Out_1
  N34: Gas_Valve_Stepper_Motor.C, Stepper_motor_driver_(GasValve).Out_2
  N35: Gas_Valve_Stepper_Motor.B, Stepper_motor_driver_(GasValve).Out_3
  N36: Gas_Valve_Stepper_Motor.D, Stepper_motor_driver_(GasValve).Out_4
  N37: LCD_TFT_2_2".SCE, R18.Pin_0
  N38: LCD_TFT_2_2".RST, R7.Pin_0
  N39: LCD_TFT_2_2".D/C, R6.Pin_0
  N40: LCD_TFT_2_2".6_DN_(MOSI), R5.Pin_0
  N41: LCD_TFT_2_2".SCLK, R4.Pin_0
  N42: Smoke_Valve_Servo.pulse, R12.Pin_1
  N43: SD_Card_(in_LCD_panel).CS, R19.Pin_0
  N44: Thermocouple.pin14, Thermocouple_2.1

custom parts:
  : Nokia 5110 LCD with 8 pin. It's a 45mm*45mm module part. Description: The Nokia 5110 is a basic graphic LCD screen for lots of applications. It was originally intended for as a cell phone screen. This one is mounted on an easy to solder PCB. It uses the PCD8544 controller. The PCD8544 is a low power CMOS LCD controller/driver, designed to drive a graphic display of 48 rows and 84 columns. All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
